# Fritzing sketch Pot_Exercise (saved by Fritzing 0.8.7b)
breadboards: 1

parts:
  part = Arduino Uno (Rev3)
  R1 = Trimmer Potentiometer [maximum_resistance=10kΩ package=THT]

nets:
  N1: part.A0, R1.wiper
  N2: part.GND, R1.leg1
  N3: part.5V, R1.leg2
